# Fritzing sketch wiring (saved by Fritzing 0.9.3b)
breadboards: 1

parts:
  Raspberry_Pi1 = Raspberry Pi 2
  R1 = Resistor [tolerance=±5% resistance=10k package="0402 [SMD]"]
  R2 = Resistor [tolerance=±5% resistance=10k package="0402 [SMD]"]
  S4 = Magnetic Door Switch [package=reed_switch_plastic]
  S5 = Magnetic Door Switch [package=reed_switch_plastic]

nets:
  N1: Raspberry_Pi1.3v3, R1.Pin_0, R2.Pin_0
  N2: Raspberry_Pi1.GND, S4.2, S5.2
  N3: Raspberry_Pi1.GPIO17, R1.Pin_1, S4.1
  N4: Raspberry_Pi1.GPIO27, R2.Pin_1, S5.1
